// Logisim project ula8bits.circ as structural Verilog: 3 circuits, main circuit main
// ULA8SAIDAS
module main (
  input  A0,
  input  B0,
  input  A1,
  input  B1,
  input  A2,
  input  B2,
  input  A3,
  input  B3,
  input  A4,
  input  B4,
  input  A5,
  input  B5,
  input  A6,
  input  B6,
  input  A7,
  input  B7,
  input  INA,
  input  ENA,
  input  ENB,
  input  F1,
  input  F0,
  input  INCA,
  output VAI_UM,
  output S0,
  output S1,
  output S2,
  output S3,
  output S4,
  output S5,
  output S6,
  output S7
);

  wire ula1bit_1_vai_um, ula1bit_2_vai_um, ula1bit_3_vai_um, ula1bit_4_vai_um, ula1bit_5_vai_um,
       ula1bit_6_vai_um, ula1bit_7_vai_um;

  ULA1bit ula1bit_1 (
    .INVA(INA), .A(A0), .ENA(ENA), .B(B0), .ENB(ENB), .F0(F0), .F1(F1), .VEM_UM(INCA),
    .VAI_UM(ula1bit_1_vai_um), .\SAÍDA (S0));
  ULA1bit ula1bit_2 (
    .INVA(INA), .A(A1), .ENA(ENA), .B(B1), .ENB(ENB), .F0(F0), .F1(F1), .VEM_UM(ula1bit_1_vai_um),
    .VAI_UM(ula1bit_2_vai_um), .\SAÍDA (S1));
  ULA1bit ula1bit_3 (
    .INVA(INA), .A(A2), .ENA(ENA), .B(B2), .ENB(ENB), .F0(F0), .F1(F1), .VEM_UM(ula1bit_2_vai_um),
    .VAI_UM(ula1bit_3_vai_um), .\SAÍDA (S2));
  ULA1bit ula1bit_4 (
    .INVA(INA), .A(A3), .ENA(ENA), .B(B3), .ENB(ENB), .F0(F0), .F1(F1), .VEM_UM(ula1bit_3_vai_um),
    .VAI_UM(ula1bit_4_vai_um), .\SAÍDA (S3));
  ULA1bit ula1bit_5 (
    .INVA(INA), .A(A4), .ENA(ENA), .B(B4), .ENB(ENB), .F0(F0), .F1(F1), .VEM_UM(ula1bit_4_vai_um),
    .VAI_UM(ula1bit_5_vai_um), .\SAÍDA (S4));
  ULA1bit ula1bit_6 (
    .INVA(INA), .A(A5), .ENA(ENA), .B(B5), .ENB(ENB), .F0(F0), .F1(F1), .VEM_UM(ula1bit_5_vai_um),
    .VAI_UM(ula1bit_6_vai_um), .\SAÍDA (S5));
  ULA1bit ula1bit_7 (
    .INVA(INA), .A(A6), .ENA(ENA), .B(B6), .ENB(ENB), .F0(F0), .F1(F1), .VEM_UM(ula1bit_6_vai_um),
    .VAI_UM(ula1bit_7_vai_um), .\SAÍDA (S6));
  ULA1bit ula1bit_8 (
    .INVA(INA), .A(A7), .ENA(ENA), .B(B7), .ENB(ENB), .F0(F0), .F1(F1), .VEM_UM(ula1bit_7_vai_um),
    .VAI_UM(VAI_UM), .\SAÍDA (S7));

  // Notes on the sheet:
  //   ULA com 16 entradas de dados (A e B) e 48 entradas de controle (INA, ENA, ENB, F1, F0)  
endmodule

module ULA1bit (
  input  VEM_UM,
  input  INVA,
  input  A,
  input  ENA,
  input  B,
  input  ENB,
  input  F0,
  input  F1,
  output \SAÍDA ,
  output VAI_UM
);

  wire and_1_out, and_2_out, and_3_out, and_4_out, and_5_out, and_6_out, and_7_out, and_8_out, and_9_out,
       and_10_out, and_11_out, and_12_out, and_13_out, not_1_out, not_2_out, not_3_out, not_4_out, not_5_out,
       or_1_out, xor_1_out, xor_2_out, xor_3_out;

  not not_1 (not_1_out, F0);
  not not_2 (not_2_out, F1);
  not not_3 (not_3_out, F0);
  not not_4 (not_4_out, F1);
  and and_1 (and_1_out, A, ENA);
  and and_2 (and_2_out, B, ENB);
  and and_3 (and_3_out, not_1_out, not_2_out);
  and and_4 (and_4_out, not_3_out, F1);
  and and_5 (and_5_out, F0, not_4_out);
  and and_6 (and_6_out, F0, F1);
  xor xor_1 (xor_1_out, INVA, and_1_out);
  and and_7 (and_7_out, xor_1_out, and_2_out);
  or or_1 (or_1_out, xor_1_out, and_2_out);
  not not_5 (not_5_out, and_2_out);
  and and_8 (and_8_out, and_7_out, and_3_out);
  and and_9 (and_9_out, or_1_out, and_4_out);
  and and_10 (and_10_out, not_5_out, and_5_out);
  and and_11 (and_11_out, and_6_out, xor_1_out, and_2_out);
  xor xor_2 (xor_2_out, and_2_out, xor_1_out);
  or or_2 (VAI_UM, and_11_out, and_12_out);
  and and_12 (and_12_out, and_6_out, xor_2_out, VEM_UM);
  xor xor_3 (xor_3_out, VEM_UM, xor_2_out);
  and and_13 (and_13_out, xor_3_out, and_6_out);
  or or_3 (\SAÍDA , and_8_out, and_9_out, and_10_out, and_13_out);

  // Notes on the sheet:
  //   AB
  //   A+B
  //   _
  //   B
  //   SOMA
endmodule

module ula8saidas (
  input  A0,
  input  A1,
  input  A2,
  input  A3,
  input  A4,
  input  A5,
  input  A6,
  input  A7,
  input  B0,
  input  B1,
  input  B2,
  input  B3,
  input  B4,
  input  B5,
  input  B6,
  input  B7,
  input  INA,
  input  ENA,
  input  ENB,
  input  F1,
  input  F2,
  input  in_22,
  input  S0,
  input  S1,
  input  S2,
  input  S3,
  input  S4,
  input  S5,
  input  S6,
  input  S7,
  output out_31
);

  main main_1 (
    .INA(INA), .ENA(ENA), .ENB(ENB), .F1(F1), .F0(F2), .INCA(in_22), .A0(A0), .B0(B0), .A1(A1), .B1(B1),
    .A2(A2), .B2(B2), .A3(A3), .B3(B3), .A4(A4), .B4(B4), .A5(A5), .B5(B5), .A6(A6), .B6(B6), .A7(A7),
    .B7(B7), .S0(S0), .S1(S1), .S2(S2), .S3(S3), .S4(S4), .S5(S5), .S6(S6), .S7(S7), .VAI_UM(out_31));
endmodule
